# Fritzing sketch AGOpensteer (saved by Fritzing 0.9.3b)

parts:
  Part2 = Arduino Nano (Rev3.0)
  Part1 = Monster Moto Shield
  S1 = Taiway 100-SP-X-T1 SPDT Miniature Toggle Switch [part_number=100-SP-X-T1-0-0-B1-M2 package=THT]
  M1 = DC Motor
  Part3 = 9-DOF Absolute Orientation IMU Fusion Breakout - BNO055
  U1 = Sharp PC817 [package=THT]
  U2 = Vibration Motor- ROB-08449 [package=vibe-motor-10mm]
  U3 = Vibration Motor- ROB-08449 [package=vibe-motor-10mm]
  M3 = Stepper Motor - Bipolar
  F1 = FUSE [package=fuse_5mm]
  F2 = FUSE [package=fuse_5mm]
  J3 = female pin header, 2 pins [form="♀ (female)"]
  U38 = POT [package=pot_mammoth]
  M4 = DC Motor
  S23 = Taiway 100-SP-X-T1 SPDT Miniature Toggle Switch [part_number=100-SP-X-T1-0-0-B1-M2 package=THT]
  U39 = ENCODER_2LED [package=encoder_led_2]
  Part33 = SeeedStudio Can-Bus Shield
  U40 = ENCODER_2LED [package=encoder_led_2]
  U41 = PCF8574 [package="DIP16 [THT]"]
  U42 = RELAY [package=relay-jzc]
  U43 = RELAY [package=relay-jzc]
  U44 = RELAY [package=relay-jzc]
  U45 = RELAY [package=relay-jzc]
  U46 = RELAY [package=relay-jzc]
  U47 = RELAY [package=relay-jzc]
  U48 = RELAY [package=relay-jzc]
  U49 = RELAY [package=relay-jzc]
  U50 = PCF8574 [package="DIP16 [THT]"]
  U51 = RELAY [package=relay-jzc]
  U52 = RELAY [package=relay-jzc]
  U53 = RELAY [package=relay-jzc]
  U54 = RELAY [package=relay-jzc]
  U55 = RELAY [package=relay-jzc]
  U56 = RELAY [package=relay-jzc]
  U57 = RELAY [package=relay-jzc]
  U58 = RELAY [package=relay-jzc]
  U59 = PCF8574 [package="DIP16 [THT]"]
  S24 = Taiway 100-SP-X-T1 SPDT Miniature Toggle Switch [part_number=100-SP-X-T1-0-0-B1-M2 package=THT]
  S25 = Taiway 100-SP-X-T1 SPDT Miniature Toggle Switch [part_number=100-SP-X-T1-0-0-B1-M2 package=THT]
  S26 = Taiway 100-SP-X-T1 SPDT Miniature Toggle Switch [part_number=100-SP-X-T1-0-0-B1-M2 package=THT]
  S27 = Taiway 100-SP-X-T1 SPDT Miniature Toggle Switch [part_number=100-SP-X-T1-0-0-B1-M2 package=THT]
  S28 = Taiway 100-SP-X-T1 SPDT Miniature Toggle Switch [part_number=100-SP-X-T1-0-0-B1-M2 package=THT]
  S29 = Taiway 100-SP-X-T1 SPDT Miniature Toggle Switch [part_number=100-SP-X-T1-0-0-B1-M2 package=THT]
  S30 = Taiway 100-SP-X-T1 SPDT Miniature Toggle Switch [part_number=100-SP-X-T1-0-0-B1-M2 package=THT]
  S31 = Taiway 100-SP-X-T1 SPDT Miniature Toggle Switch [part_number=100-SP-X-T1-0-0-B1-M2 package=THT]
  F3 = FUSE [package=fuse_5mm]

nets:
  N1: Part2.D1/TX, Part1.RX
  N2: Part2.D0/RX, Part1.TX
  N3: Part2.RESET, Part1.RES
  N4: Part2.D2, Part1.D2, U39.B
  N5: Part2.D3, Part1.D3, U40.C
  N6: Part2.D4, Part1.INA2_-_D4
  N7: Part2.D5, Part1.PWM1_-_D5
  N8: Part2.D6, Part1.PWM2_-_D6
  N9: Part2.D7, Part1.INA1_-_D7
  N10: Part2.D8, Part1.INB1_-_D8
  N11: Part2.D9, Part1.INB2_-_D9
  N12: Part2.D10, Part1.D10, Part33.SS
  N13: Part2.D11/MOSI, Part1.D11, Part33.MOSI
  N14: Part2.D12/MISO, Part1.D12, Part33.MISO
  VIN: Part2.VIN, Part1.VIN, U1.Pin_1, F2.1
  GND: Part2.GND, Part1.GND, Part1.GND_-_GND@0, Part1.GND_-_GND@1, Part1.GND_-_GND@2, S1.L1, Part3.GND, U1.Pin_2, U38.E, U39.SW, Part33.GND, U40.SW, U41.GND, U43.MAIN, U50.GND, U52.MAIN, U59.GND, S24.L2, S25.L2, S26.L2, S27.L2, S28.L2, S29.L2, S30.L2, S31.L2
  5V: Part2.5V, Part1.5V, Part3.5.0V, U38.S, S23.L1, U39.C, Part33.5V, U40.-, U41.VCC, U48.MAIN, U50.VCC, U57.MAIN, U59.VCC, S24.L1, S25.L1, S26.L1, S27.L1, S28.L1, S29.L1, S30.L1, S31.L1, F3.1
  N15: Part2.A7, U1.Pin_3, J3.pin2
  N16: Part2.A6, J3.pin1, S23.COM
  N17: Part2.A5, Part1.A5, Part3.SCL_5V, U41.SCL, U50.SCL, U59.INT, U59.SCL
  N18: Part2.A4, Part1.A4, Part3.SDA_5V, U41.SDA, U50.SDA, U59.SDA
  N19: Part2.A3, Part1.CS2_-_A3
  N20: Part2.A2, Part1.CS1_-_A2
  N21: Part2.A1, S1.L2
  N22: Part2.A0, U38.A, U40.B
  3V3: Part2.3V3, Part1.3.3V
  N23: Part2.D13/SCK, Part1.D13, Part33.SCK
  N24: Part1.OUTA1, M1.pin_1, U3.-, M3.A
  N25: Part1.OUTB1, M1.pin_2, U3.+, M3.C
  N26: Part1.OUTA2, U2.-, M3.B, M4.pin_1
  N27: Part1.OUTB2, U2.+, M3.D, M4.pin_2
  N28: Part1.VCC, F1.1
  N29: Part1.EN1_-_A0, Part1.EN2_-_A1, S1.COM
  N30: U41.A3, U41.P0, U43.COIL1
  N31: U41.P1, U45.MAIN, U45.COIL1
  N32: U41.P2, U47.MAIN, U47.COIL1
  N33: U41.P3, U49.COIL1
  N34: U41.P4, U42.MAIN, U42.COIL1
  N35: U41.P5, U44.MAIN, U44.COIL1
  N36: U41.P6, U46.MAIN, U46.COIL1
  N37: U41.P7, U48.COIL1
  N38: U50.A3, U50.P0, U52.COIL1
  N39: U50.P1, U54.MAIN, U54.COIL1
  N40: U50.P2, U56.MAIN, U56.COIL1
  N41: U50.P3, U58.COIL1
  N42: U50.P4, U51.COIL1
  N43: U50.P5, U53.MAIN, U53.COIL1
  N44: U50.P6, U55.MAIN, U55.COIL1
  N45: U50.P7, U57.COIL1
  N46: U59.P0, S31.COM
  N47: U59.P1, S30.COM
  N48: U59.P2, S29.COM
  N49: U59.P3, S28.COM
  N50: U59.P4, S24.COM
  N51: U59.P5, S25.COM
  N52: U59.P6, S26.COM
  N53: U59.P7, S27.COM

notes:
  Steeringangle Sensor
  IMU BNO055
  Stepper Motor
  PWM Valve (single/dual)
  DC Motor (single/dual)
  Inclinometer NSDOG2
  Motor Shield
  Autosteer Switch 0-1
  ARDUINO PINOUT
  A0 Steering Sensor ( Steeringangle EncB)
  A1 Autosteer Switch (Also motors enabled)
  A2 Current Sence Motor 1 (0.13V / AMP)
  A3 Current Sence Motor 2 (0.13V / AMP)
  A4 I2C SDA (IMU, Port Expanders)
  A5 I2C SCL (IMU, Port Expanders)
  A6 Workswtich
  A7 Inclinometer Roll
  D0 Serial RX
  D1 Serial TX
  D2 Interrupt Steeringangle EncA
  D3 Interurpt Steeringwheel PULSE
  D4 Motor 2 Clockwise
  D5 Motor 1 PWM
  D6 Motor 2 PWM
  D7 Motor 1 Clockwise
  D8 Motor 1 Counter Clockwise
  D9 Motor 2 Counter Clockwise
  D10 SPI CS (CANBUS)
  D11 SPI MOSI (CANBUS)
  D12 SPI MISO (CANBUS)
  D13 SPI SCK (CANBUS)
  STEERING SENSOR OPTIONS
  Steering Sensor Analog
  Steering Encoder Quadrature
  Steering CANBUS Angle
  STEERING MOTOR OPTIONS
  Single stepper
  Single DC Steering motor with current sense
  Dual DC Steering motor with current sense
  Dual PWM Hydraulic steering Valve
  DANFOSS PWM Hydraulic steering Valve-
  CANBUS Steering
  STEERING ABORT OPTIONS
  AutoSteer Switch
  DC Currentlimit Detection
  Steeringwheel Pulselimit Detection
  ORIENTATION SENSOR OPTIONS
  9DOF IMU
  Roll/Tilt inclinometer (Roll Only)
  RELAY OPTIONS
  8 Section Relays
  8 Uturn Relays (6 from OAG)
  INPUT OPTIONS
  8 ON-OFF Switches
  CANBUS Shield
  Steeringwheel Pulse
  WorkSwitch 0-1
  Steeringangle encoder
  Switch Inputs
  Relays (Section / Uturn)

custom parts:
  9-DOF Absolute Orientation IMU Fusion Breakout - BNO055: A MEMS accelerometer, magnetometer and gyroscope on a single die with a high speed ARM Cortex-M0 based processor to digest all the sensor data, abstract the sensor fusion and real time requirements away, and spit out data you can use in quaternions, Euler angles or vectors.
  SeeedStudio Can-Bus Shield: This CAN-BUS Shield adopts MCP2515 CAN Bus controller with SPI interface and MCP2551 CAN transceiver to give your Arduino/Seeeduino CAN-BUS capibility. With an OBD-II converter cable added on and the OBD-II library imported, you are ready to build an onboard diagnostic device or data logger. Features Implements CAN V2.0B at up to 1 Mb/s SPI Interface up to 10 MHz Standard (11 bit) and extended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
